// Logisim project Nand2Tetris.circ as structural Verilog: 25 circuits, main circuit main
module main (
);

  wire button_1_out, clock_1_out, cpu_1_writem, display_1_out_2, display_1_out_3, display_1_out_4,
       display_1_out_5, display_1_out_6, display_1_out_7, display_1_out_8, display_1_out_9, display_1_out_10,
       display_1_out_11, display_1_out_12, display_1_out_13, display_1_out_14, display_1_out_15,
       display_1_out_16, display_1_out_17, display_1_out_18, display_1_out_19, display_1_out_20,
       display_1_out_21, display_1_out_22, display_1_out_23, display_1_out_24, display_1_out_25,
       display_1_out_26, display_1_out_27, display_1_out_28, display_1_out_29, display_1_out_30,
       display_1_out_31, display_1_out_32, display_1_out_33, display_1_out_34, display_1_out_35,
       display_1_out_36, display_1_out_37, display_1_out_38, display_1_out_39, display_1_out_40,
       display_1_out_41, not_1_out;
  wire [14:0] cpu_1_addressm, cpu_1_pc;
  wire [15:0] cpu_1_outm, ram_1_data, rom_1_data;

  // Probe on rom_1_data
  ROM #(.addrWidth(15), .dataWidth(16)) rom_1 (.addr(cpu_1_pc), .data(rom_1_data));  // open: sel
  // Probe on cpu_1_pc
  CPU cpu_1 (
    .Instruction(rom_1_data), .Data_Memory(ram_1_data), .Reset(button_1_out), .outM(cpu_1_outm),
    .writeM(cpu_1_writem), .addressM(cpu_1_addressm), .pc(cpu_1_pc));  // open: cl
  Button button_1 (.out(button_1_out));
  // Probe on cpu_1_outm
  // Probe on cpu_1_addressm
  not not_1 (not_1_out, clock_1_out);
  RAM #(.addrWidth(15), .dataWidth(16), .bus("separate")) ram_1 (
    .addr(cpu_1_addressm), .din(cpu_1_outm), .data(ram_1_data), .str(cpu_1_writem), .clk(not_1_out));  // open: sel, ld, clr
  Clock clock_1 (.out(clock_1_out));
  // Probe on ram_1_data
  _7_Segment_Display u_7_segment_display_1 (
    .g(display_1_out_2), .f(display_1_out_3), .a(display_1_out_4), .b(display_1_out_5), .e(display_1_out_22),
    .d(display_1_out_23), .c(display_1_out_24), .dp(display_1_out_25));
  _7_Segment_Display u_7_segment_display_2 (
    .g(display_1_out_6), .f(display_1_out_7), .a(display_1_out_8), .b(display_1_out_9), .e(display_1_out_26),
    .d(display_1_out_27), .c(display_1_out_28), .dp(display_1_out_29));
  _7_Segment_Display u_7_segment_display_3 (
    .g(display_1_out_10), .f(display_1_out_11), .a(display_1_out_12), .b(display_1_out_13),
    .e(display_1_out_30), .d(display_1_out_31), .c(display_1_out_32), .dp(display_1_out_33));
  _7_Segment_Display u_7_segment_display_4 (
    .g(display_1_out_14), .f(display_1_out_15), .a(display_1_out_16), .b(display_1_out_17),
    .e(display_1_out_34), .d(display_1_out_35), .c(display_1_out_36), .dp(display_1_out_37));
  Display display_1 (
    .in_1(ram_1_data), .out_2(display_1_out_2), .out_3(display_1_out_3), .out_4(display_1_out_4),
    .out_5(display_1_out_5), .out_6(display_1_out_6), .out_7(display_1_out_7), .out_8(display_1_out_8),
    .out_9(display_1_out_9), .out_10(display_1_out_10), .out_11(display_1_out_11), .out_12(display_1_out_12),
    .out_13(display_1_out_13), .out_14(display_1_out_14), .out_15(display_1_out_15),
    .out_16(display_1_out_16), .out_17(display_1_out_17), .out_18(display_1_out_18),
    .out_19(display_1_out_19), .out_20(display_1_out_20), .out_21(display_1_out_21),
    .out_22(display_1_out_22), .out_23(display_1_out_23), .out_24(display_1_out_24),
    .out_26(display_1_out_26), .out_27(display_1_out_27), .out_28(display_1_out_28),
    .out_29(display_1_out_29), .out_30(display_1_out_30), .out_31(display_1_out_31),
    .out_32(display_1_out_32), .out_33(display_1_out_33), .out_34(display_1_out_34),
    .out_35(display_1_out_35), .out_36(display_1_out_36), .out_37(display_1_out_37),
    .out_38(display_1_out_38), .out_39(display_1_out_39), .out_40(display_1_out_40),
    .out_41(display_1_out_41), .out_25(display_1_out_25));
  _7_Segment_Display u_7_segment_display_5 (
    .g(display_1_out_18), .f(display_1_out_19), .a(display_1_out_20), .b(display_1_out_21),
    .e(display_1_out_38), .d(display_1_out_39), .c(display_1_out_40), .dp(display_1_out_41));
  _7_Segment_Display u_7_segment_display_6 ();  // open: g, f, a, b, e, d, c, dp

  // Notes on the sheet:
  //   contents of rom_1 (hex, n*v repeats v):
  //   b ec10 0 f308 2 fa88 3 ffc8 2 fc10 1 f308 3 fc10 2 f088 1 fc10 3 f308 0 fc88 fc10 8 e305 2 8000 8000
endmodule

module _16bit_Adder (
  input  [15:0] in_1,
  input  [15:0] in_2,
  output [15:0] out_3
);

  wire full_adder_1_carry, full_adder_2_carry, full_adder_3_carry, full_adder_4_carry, full_adder_5_carry,
       full_adder_6_carry, full_adder_7_carry, full_adder_8_carry, full_adder_9_carry, full_adder_10_carry,
       full_adder_11_carry, full_adder_12_carry, full_adder_13_carry, full_adder_14_carry,
       full_adder_15_carry;

  Full_Adder full_adder_1 (.a(in_1[0]), .b(1'b0), .c(in_2[0]), .sum(out_3[0]), .carry(full_adder_1_carry));
  Full_Adder full_adder_2 (
    .a(full_adder_1_carry), .b(in_1[1]), .c(in_2[1]), .sum(out_3[1]), .carry(full_adder_2_carry));
  Full_Adder full_adder_3 (
    .a(full_adder_2_carry), .b(in_1[2]), .c(in_2[2]), .sum(out_3[2]), .carry(full_adder_3_carry));
  Full_Adder full_adder_4 (
    .a(full_adder_3_carry), .b(in_1[3]), .c(in_2[3]), .sum(out_3[3]), .carry(full_adder_4_carry));
  Full_Adder full_adder_5 (
    .a(full_adder_4_carry), .b(in_1[4]), .c(in_2[4]), .sum(out_3[4]), .carry(full_adder_5_carry));
  Full_Adder full_adder_6 (
    .a(full_adder_5_carry), .b(in_1[5]), .c(in_2[5]), .sum(out_3[5]), .carry(full_adder_6_carry));
  Full_Adder full_adder_7 (
    .a(full_adder_6_carry), .b(in_1[6]), .c(in_2[6]), .sum(out_3[6]), .carry(full_adder_7_carry));
  Full_Adder full_adder_8 (
    .a(full_adder_7_carry), .b(in_1[7]), .c(in_2[7]), .sum(out_3[7]), .carry(full_adder_8_carry));
  Full_Adder full_adder_9 (
    .a(full_adder_8_carry), .b(in_1[8]), .c(in_2[8]), .sum(out_3[8]), .carry(full_adder_9_carry));
  Full_Adder full_adder_10 (
    .a(full_adder_9_carry), .b(in_1[9]), .c(in_2[9]), .sum(out_3[9]), .carry(full_adder_10_carry));
  Full_Adder full_adder_11 (
    .a(full_adder_10_carry), .b(in_1[10]), .c(in_2[10]), .sum(out_3[10]), .carry(full_adder_11_carry));
  Full_Adder full_adder_12 (
    .a(full_adder_11_carry), .b(in_1[11]), .c(in_2[11]), .sum(out_3[11]), .carry(full_adder_12_carry));
  Full_Adder full_adder_13 (
    .a(full_adder_12_carry), .b(in_1[12]), .c(in_2[12]), .sum(out_3[12]), .carry(full_adder_13_carry));
  Full_Adder full_adder_14 (
    .a(full_adder_13_carry), .b(in_1[13]), .c(in_2[13]), .sum(out_3[13]), .carry(full_adder_14_carry));
  Full_Adder full_adder_15 (
    .a(full_adder_14_carry), .b(in_1[14]), .c(in_2[14]), .sum(out_3[14]), .carry(full_adder_15_carry));
  Full_Adder full_adder_16 (.a(full_adder_15_carry), .b(in_1[15]), .c(in_2[15]), .sum(out_3[15]));  // open: carry
endmodule

module Full_Adder (
  input  a,
  input  b,
  input  c,
  output sum,
  output carry
);

  wire half_adder_1_carry, half_adder_1_sum, half_adder_2_carry;

  Half_Adder half_adder_1 (.a(a), .b(b), .sum(half_adder_1_sum), .carry(half_adder_1_carry));
  Half_Adder half_adder_2 (.a(half_adder_1_sum), .b(c), .sum(sum), .carry(half_adder_2_carry));
  or or_1 (carry, half_adder_2_carry, half_adder_1_carry);
endmodule

module Half_Adder (
  input  a,
  input  b,
  output sum,
  output carry
);

  xor xor_1 (sum, a, b);
  and and_1 (carry, a, b);
endmodule

module _4bit_Adder (
  input  [3:0] a,
  input  [3:0] b,
  output [3:0] c
);

  wire full_adder_1_carry, full_adder_2_carry, full_adder_3_carry;

  Full_Adder full_adder_1 (.a(1'b0), .b(a[0]), .c(b[0]), .sum(c[0]), .carry(full_adder_1_carry));
  Full_Adder full_adder_2 (.a(full_adder_1_carry), .b(a[1]), .c(b[1]), .sum(c[1]), .carry(full_adder_2_carry));
  Full_Adder full_adder_3 (.a(full_adder_2_carry), .b(a[2]), .c(b[2]), .sum(c[2]), .carry(full_adder_3_carry));
  Full_Adder full_adder_4 (.a(full_adder_3_carry), .b(a[3]), .c(b[3]), .sum(c[3]));  // open: carry
endmodule

module _4bit_Bump (
  input  [3:0] a,
  output [3:0] c
);

  wire half_adder_1_carry, half_adder_2_carry, half_adder_3_carry;

  Half_Adder half_adder_1 (.a(1'b1), .b(a[0]), .sum(c[0]), .carry(half_adder_1_carry));
  Half_Adder half_adder_2 (.a(half_adder_1_carry), .b(a[1]), .sum(c[1]), .carry(half_adder_2_carry));
  Half_Adder half_adder_3 (.a(half_adder_2_carry), .b(a[2]), .sum(c[2]), .carry(half_adder_3_carry));
  Half_Adder half_adder_4 (.a(half_adder_3_carry), .b(a[3]), .sum(c[3]));  // open: carry
endmodule

module ALU (
  input  zx,
  input  nx,
  input  [15:0] x,
  input  f,
  input  no,
  input  zy,
  input  ny,
  input  [15:0] y,
  output [15:0] y_2,
  output ng,
  output zr
);

  wire [15:0] adder_1_out, and_1_out, multiplexer_1_out, multiplexer_2_out, multiplexer_3_out,
       multiplexer_4_out, multiplexer_5_out, not_1_out, not_2_out, not_3_out;

  Multiplexer_part #(.width(16)) multiplexer_1 (
    .in0(x), .in1({16{1'b0}}), .out(multiplexer_1_out), .sel(zx));  // open: en
  Multiplexer_part #(.width(16)) multiplexer_2 (
    .in0(y), .in1({16{1'b0}}), .out(multiplexer_2_out), .sel(zy));  // open: en
  assign not_1_out = ~multiplexer_1_out;  // NOT_Gate not_1, 16 bits wide
  assign not_2_out = ~multiplexer_2_out;  // NOT_Gate not_2, 16 bits wide
  // Probe on multiplexer_3_out
  Multiplexer_part #(.width(16)) multiplexer_3 (
    .in0(multiplexer_1_out), .in1(not_1_out), .out(multiplexer_3_out), .sel(nx));  // open: en
  Multiplexer_part #(.width(16)) multiplexer_4 (
    .in0(multiplexer_2_out), .in1(not_2_out), .out(multiplexer_4_out), .sel(ny));  // open: en
  // Probe on multiplexer_4_out
  assign and_1_out = multiplexer_3_out & multiplexer_4_out;  // AND_Gate and_1, 16 bits wide
  Adder #(.width(16)) adder_1 (.a(multiplexer_3_out), .b(multiplexer_4_out), .out(adder_1_out));  // open: cin, cout
  Multiplexer_part #(.width(16)) multiplexer_5 (
    .in0(and_1_out), .in1(adder_1_out), .out(multiplexer_5_out), .sel(f));  // open: en
  // Probe on multiplexer_5_out
  // Probe on {ng, y_2[14:0]}
  Multiplexer_part #(.width(16)) multiplexer_6 (
    .in0(multiplexer_5_out), .in1(not_3_out), .out({ng, y_2[14:0]}), .sel(no));  // open: en
  assign not_3_out = ~multiplexer_5_out;  // NOT_Gate not_3, 16 bits wide
  // Probe on {ng, y_2[14:0]}
  nor nor_1 (zr, y_2[0], y_2[1], y_2[2], y_2[3], y_2[4], y_2[5], y_2[6], y_2[7], y_2[8], y_2[9], y_2[10], y_2[11], y_2[12], y_2[13], y_2[14], ng);

  assign y_2[15] = ng;
endmodule

module ClockedData_Flip_Flop (
  input  in_1,
  input  in_2,
  output out_3
);

  wire nand_1_out, nand_2_out, nand_4_out, not_1_out;

  not not_1 (not_1_out, in_1);
  nand nand_1 (nand_1_out, in_2, in_1);
  nand nand_2 (nand_2_out, not_1_out, in_2);
  nand nand_3 (out_3, nand_1_out, nand_4_out);
  nand nand_4 (nand_4_out, out_3, nand_2_out);
endmodule

module _1_bit_Register (
  input  load,
  input  in_2,
  input  data,
  output out_4
);

  wire multiplexer_1_out;

  Multiplexer_part multiplexer_1 (.in0(out_4), .in1(data), .out(multiplexer_1_out), .sel(load));  // open: en
  ClockedData_Flip_Flop clockeddata_flip_flop_1 (.in_1(multiplexer_1_out), .out_3(out_4), .in_2(in_2));
endmodule

module _16bit_Register (
  input  load,
  input  cl,
  input  [15:0] in_3,
  output [15:0] out_4
);

  // Probe on in_3
  _1_bit_Register u_1_bit_register_1 (.data(in_3[0]), .out_4(out_4[0]), .load(load), .in_2(cl));
  _1_bit_Register u_1_bit_register_2 (.data(in_3[1]), .out_4(out_4[1]), .load(load), .in_2(cl));
  _1_bit_Register u_1_bit_register_3 (.data(in_3[2]), .out_4(out_4[2]), .load(load), .in_2(cl));
  _1_bit_Register u_1_bit_register_4 (.data(in_3[3]), .out_4(out_4[3]), .load(load), .in_2(cl));
  _1_bit_Register u_1_bit_register_5 (.data(in_3[4]), .out_4(out_4[4]), .load(load), .in_2(cl));
  _1_bit_Register u_1_bit_register_6 (.data(in_3[5]), .out_4(out_4[5]), .load(load), .in_2(cl));
  _1_bit_Register u_1_bit_register_7 (.data(in_3[6]), .out_4(out_4[6]), .load(load), .in_2(cl));
  _1_bit_Register u_1_bit_register_8 (.data(in_3[7]), .out_4(out_4[7]), .load(load), .in_2(cl));
  _1_bit_Register u_1_bit_register_9 (.data(in_3[8]), .out_4(out_4[8]), .load(load), .in_2(cl));
  _1_bit_Register u_1_bit_register_10 (.data(in_3[9]), .out_4(out_4[9]), .load(load), .in_2(cl));
  _1_bit_Register u_1_bit_register_11 (.data(in_3[10]), .out_4(out_4[10]), .load(load), .in_2(cl));
  _1_bit_Register u_1_bit_register_12 (.data(in_3[11]), .out_4(out_4[11]), .load(load), .in_2(cl));
  _1_bit_Register u_1_bit_register_13 (.data(in_3[12]), .out_4(out_4[12]), .load(load), .in_2(cl));
  _1_bit_Register u_1_bit_register_14 (.data(in_3[13]), .out_4(out_4[13]), .load(load), .in_2(cl));
  _1_bit_Register u_1_bit_register_15 (.data(in_3[14]), .out_4(out_4[14]), .load(load), .in_2(cl));
  _1_bit_Register u_1_bit_register_16 (.data(in_3[15]), .out_4(out_4[15]), .load(load), .in_2(cl));
endmodule

module _4_RAM (
  input  cl,
  input  load,
  input  [15:0] in,
  input  [1:0] address,
  output [15:0] out
);

  wire demultiplexer_1_out0, demultiplexer_1_out1, demultiplexer_1_out2, demultiplexer_1_out3;
  wire [15:0] n16bit_register_1_out_4, n16bit_register_2_out_4, n16bit_register_3_out_4,
       n16bit_register_4_out_4;

  Clock clock_1 ();  // open: out
  Demultiplexer_part #(.select(2), .enable("false")) demultiplexer_1 (
    .out0(demultiplexer_1_out0), .out1(demultiplexer_1_out1), .out2(demultiplexer_1_out2),
    .out3(demultiplexer_1_out3), .in(load), .sel(address));
  _16bit_Register u_16bit_register_1 (.in_3(in), .out_4(n16bit_register_1_out_4), .load(demultiplexer_1_out3), .cl(cl));
  _16bit_Register u_16bit_register_2 (.in_3(in), .out_4(n16bit_register_2_out_4), .load(demultiplexer_1_out2), .cl(cl));
  _16bit_Register u_16bit_register_3 (.in_3(in), .out_4(n16bit_register_3_out_4), .load(demultiplexer_1_out1), .cl(cl));
  _16bit_Register u_16bit_register_4 (.in_3(in), .out_4(n16bit_register_4_out_4), .load(demultiplexer_1_out0), .cl(cl));
  // Probe on out
  Multiplexer_part #(.select(2), .width(16), .enable("false")) multiplexer_1 (
    .in0(n16bit_register_4_out_4), .in1(n16bit_register_3_out_4), .in2(n16bit_register_2_out_4),
    .in3(n16bit_register_1_out_4), .out(out), .sel(address));
endmodule

module Counter (
  input  inc,
  input  load,
  input  clr,
  input  [14:0] in,
  output [14:0] out
);

  wire and_1_out, and_2_out, and_3_out, and_4_out, and_5_out, and_6_out, and_7_out, and_8_out, and_9_out,
       and_10_out, and_11_out, and_12_out, and_13_out, and_14_out, and_15_out, and_16_out, and_17_out,
       and_18_out, and_19_out, and_20_out, and_21_out, and_22_out, and_23_out, and_24_out, and_25_out,
       and_26_out, and_27_out, and_28_out, and_29_out, and_30_out, and_31_out, and_32_out, and_33_out,
       and_34_out, and_35_out, and_36_out, and_37_out, and_38_out, and_39_out, and_40_out, and_41_out,
       and_42_out, and_43_out, and_44_out, clock_1_out, nand_1_out, nand_2_out, nand_3_out, nand_4_out,
       nand_5_out, nand_6_out, nand_7_out, nand_8_out, nand_9_out, nand_10_out, nand_11_out, nand_12_out,
       nand_13_out, nand_14_out, nand_15_out, nand_16_out, nand_17_out, nand_18_out, nand_19_out,
       nand_20_out, nand_21_out, nand_22_out, nand_23_out, nand_24_out, nand_25_out, nand_26_out,
       nand_27_out, nand_28_out, nand_29_out, nand_30_out, or_1_out, or_2_out, or_3_out, or_4_out, or_5_out,
       or_6_out, or_7_out, or_8_out, or_9_out, or_10_out, or_11_out, or_12_out, or_13_out, or_14_out,
       or_15_out, or_16_out;

  and and_1 (and_1_out, inc, out[0]);
  and and_2 (and_2_out, and_1_out, out[1]);
  and and_3 (and_3_out, and_2_out, out[2]);
  and and_4 (and_4_out, and_3_out, out[3]);
  and and_5 (and_5_out, and_4_out, out[4]);
  and and_6 (and_6_out, and_5_out, out[5]);
  and and_7 (and_7_out, and_6_out, out[6]);
  and and_8 (and_8_out, and_7_out, out[7]);
  and and_9 (and_9_out, and_8_out, out[8]);
  and and_10 (and_10_out, and_9_out, out[9]);
  and and_11 (and_11_out, and_10_out, out[10]);
  and and_12 (and_12_out, and_11_out, out[11]);
  and and_13 (and_13_out, and_12_out, out[12]);
  and and_14 (and_14_out, and_13_out, out[13]);
  nand nand_1 (nand_1_out, load, nand_2_out);
  or or_1 (or_1_out, inc, load);
  nand nand_2 (nand_2_out, in[0], load);
  nand nand_3 (nand_3_out, load, nand_4_out);
  or or_2 (or_2_out, and_1_out, load);
  nand nand_4 (nand_4_out, in[1], load);
  nand nand_5 (nand_5_out, load, nand_6_out);
  or or_3 (or_3_out, and_2_out, load);
  nand nand_6 (nand_6_out, in[2], load);
  nand nand_7 (nand_7_out, load, nand_8_out);
  or or_4 (or_4_out, and_3_out, load);
  nand nand_8 (nand_8_out, in[3], load);
  nand nand_9 (nand_9_out, load, nand_10_out);
  or or_5 (or_5_out, and_4_out, load);
  nand nand_10 (nand_10_out, in[4], load);
  nand nand_11 (nand_11_out, load, nand_12_out);
  or or_6 (or_6_out, and_5_out, load);
  nand nand_12 (nand_12_out, in[5], load);
  nand nand_13 (nand_13_out, load, nand_14_out);
  or or_7 (or_7_out, and_6_out, load);
  nand nand_14 (nand_14_out, in[6], load);
  nand nand_15 (nand_15_out, load, nand_16_out);
  or or_8 (or_8_out, and_7_out, load);
  nand nand_16 (nand_16_out, in[7], load);
  nand nand_17 (nand_17_out, load, nand_18_out);
  or or_9 (or_9_out, and_8_out, load);
  nand nand_18 (nand_18_out, in[8], load);
  nand nand_19 (nand_19_out, load, nand_20_out);
  or or_10 (or_10_out, and_9_out, load);
  nand nand_20 (nand_20_out, in[9], load);
  nand nand_21 (nand_21_out, load, nand_22_out);
  or or_11 (or_11_out, and_10_out, load);
  nand nand_22 (nand_22_out, in[10], load);
  nand nand_23 (nand_23_out, load, nand_24_out);
  or or_12 (or_12_out, and_11_out, load);
  nand nand_24 (nand_24_out, in[11], load);
  nand nand_25 (nand_25_out, load, nand_26_out);
  or or_13 (or_13_out, and_12_out, load);
  nand nand_26 (nand_26_out, in[12], load);
  nand nand_27 (nand_27_out, load, nand_28_out);
  or or_14 (or_14_out, and_13_out, load);
  nand nand_28 (nand_28_out, in[13], load);
  nand nand_29 (nand_29_out, load, nand_30_out);
  or or_15 (or_15_out, and_14_out, load);
  nand nand_30 (nand_30_out, in[14], load);
  Clock clock_1 (.out(clock_1_out));
  or or_16 (or_16_out, clock_1_out, clr);
  and and_15 (and_15_out, nand_1_out, or_1_out);
  and and_16 (and_16_out, or_1_out, nand_2_out);
  and and_17 (and_17_out, nand_3_out, or_2_out);
  and and_18 (and_18_out, or_2_out, nand_4_out);
  and and_19 (and_19_out, nand_5_out, or_3_out);
  and and_20 (and_20_out, or_3_out, nand_6_out);
  and and_21 (and_21_out, nand_7_out, or_4_out);
  and and_22 (and_22_out, or_4_out, nand_8_out);
  and and_23 (and_23_out, nand_9_out, or_5_out);
  and and_24 (and_24_out, or_5_out, nand_10_out);
  and and_25 (and_25_out, nand_11_out, or_6_out);
  and and_26 (and_26_out, or_6_out, nand_12_out);
  and and_27 (and_27_out, nand_13_out, or_7_out);
  and and_28 (and_28_out, or_7_out, nand_14_out);
  and and_29 (and_29_out, nand_15_out, or_8_out);
  and and_30 (and_30_out, or_8_out, nand_16_out);
  and and_31 (and_31_out, nand_17_out, or_9_out);
  and and_32 (and_32_out, or_9_out, nand_18_out);
  and and_33 (and_33_out, nand_19_out, or_10_out);
  and and_34 (and_34_out, or_10_out, nand_20_out);
  and and_35 (and_35_out, nand_21_out, or_11_out);
  and and_36 (and_36_out, or_11_out, nand_22_out);
  and and_37 (and_37_out, nand_23_out, or_12_out);
  and and_38 (and_38_out, or_12_out, nand_24_out);
  and and_39 (and_39_out, nand_25_out, or_13_out);
  and and_40 (and_40_out, or_13_out, nand_26_out);
  and and_41 (and_41_out, nand_27_out, or_14_out);
  and and_42 (and_42_out, or_14_out, nand_28_out);
  and and_43 (and_43_out, nand_29_out, or_15_out);
  and and_44 (and_44_out, or_15_out, nand_30_out);
  J_K_Flip_Flop j_k_ff_1 (
    .J(and_15_out), .clk(or_16_out), .K(and_16_out), .Q(out[0]), .reset(clr));  // open: Qn, preset, en
  J_K_Flip_Flop j_k_ff_2 (
    .J(and_17_out), .clk(or_16_out), .K(and_18_out), .Q(out[1]), .reset(clr));  // open: Qn, preset, en
  J_K_Flip_Flop j_k_ff_3 (
    .J(and_19_out), .clk(or_16_out), .K(and_20_out), .Q(out[2]), .reset(clr));  // open: Qn, preset, en
  J_K_Flip_Flop j_k_ff_4 (
    .J(and_21_out), .clk(or_16_out), .K(and_22_out), .Q(out[3]), .reset(clr));  // open: Qn, preset, en
  J_K_Flip_Flop j_k_ff_5 (
    .J(and_23_out), .clk(or_16_out), .K(and_24_out), .Q(out[4]), .reset(clr));  // open: Qn, preset, en
  J_K_Flip_Flop j_k_ff_6 (
    .J(and_25_out), .clk(or_16_out), .K(and_26_out), .Q(out[5]), .reset(clr));  // open: Qn, preset, en
  J_K_Flip_Flop j_k_ff_7 (
    .J(and_27_out), .clk(or_16_out), .K(and_28_out), .Q(out[6]), .reset(clr));  // open: Qn, preset, en
  J_K_Flip_Flop j_k_ff_8 (
    .J(and_29_out), .clk(or_16_out), .K(and_30_out), .Q(out[7]), .reset(clr));  // open: Qn, preset, en
  J_K_Flip_Flop j_k_ff_9 (
    .J(and_31_out), .clk(or_16_out), .K(and_32_out), .Q(out[8]), .reset(clr));  // open: Qn, preset, en
  J_K_Flip_Flop j_k_ff_10 (
    .J(and_33_out), .clk(or_16_out), .K(and_34_out), .Q(out[9]), .reset(clr));  // open: Qn, preset, en
  J_K_Flip_Flop j_k_ff_11 (
    .J(and_35_out), .clk(or_16_out), .K(and_36_out), .Q(out[10]), .reset(clr));  // open: Qn, preset, en
  J_K_Flip_Flop j_k_ff_12 (
    .J(and_37_out), .clk(or_16_out), .K(and_38_out), .Q(out[11]), .reset(clr));  // open: Qn, preset, en
  J_K_Flip_Flop j_k_ff_13 (
    .J(and_39_out), .clk(or_16_out), .K(and_40_out), .Q(out[12]), .reset(clr));  // open: Qn, preset, en
  J_K_Flip_Flop j_k_ff_14 (
    .J(and_41_out), .clk(or_16_out), .K(and_42_out), .Q(out[13]), .reset(clr));  // open: Qn, preset, en
  J_K_Flip_Flop j_k_ff_15 (
    .J(and_43_out), .clk(or_16_out), .K(and_44_out), .Q(out[14]), .reset(clr));  // open: Qn, preset, en
endmodule

module _16_Bump (
  input  [15:0] a,
  output [15:0] c
);

  wire half_adder_1_carry, half_adder_2_carry, half_adder_3_carry, half_adder_4_carry, half_adder_5_carry,
       half_adder_6_carry, half_adder_7_carry, half_adder_8_carry, half_adder_9_carry, half_adder_10_carry,
       half_adder_11_carry, half_adder_12_carry, half_adder_13_carry, half_adder_14_carry,
       half_adder_15_carry;

  Half_Adder half_adder_1 (.a(1'b1), .b(a[0]), .sum(c[0]), .carry(half_adder_1_carry));
  Half_Adder half_adder_2 (.a(half_adder_1_carry), .b(a[1]), .sum(c[1]), .carry(half_adder_2_carry));
  Half_Adder half_adder_3 (.a(half_adder_2_carry), .b(a[2]), .sum(c[2]), .carry(half_adder_3_carry));
  Half_Adder half_adder_4 (.a(half_adder_3_carry), .b(a[3]), .sum(c[3]), .carry(half_adder_4_carry));
  Half_Adder half_adder_5 (.a(half_adder_4_carry), .b(a[4]), .sum(c[4]), .carry(half_adder_5_carry));
  Half_Adder half_adder_6 (.a(half_adder_5_carry), .b(a[5]), .sum(c[5]), .carry(half_adder_6_carry));
  Half_Adder half_adder_7 (.a(half_adder_6_carry), .b(a[6]), .sum(c[6]), .carry(half_adder_7_carry));
  Half_Adder half_adder_8 (.a(half_adder_7_carry), .b(a[7]), .sum(c[7]), .carry(half_adder_8_carry));
  Half_Adder half_adder_9 (.a(half_adder_8_carry), .b(a[8]), .sum(c[8]), .carry(half_adder_9_carry));
  Half_Adder half_adder_10 (.a(half_adder_9_carry), .b(a[9]), .sum(c[9]), .carry(half_adder_10_carry));
  Half_Adder half_adder_11 (.a(half_adder_10_carry), .b(a[10]), .sum(c[10]), .carry(half_adder_11_carry));
  Half_Adder half_adder_12 (.a(half_adder_11_carry), .b(a[11]), .sum(c[11]), .carry(half_adder_12_carry));
  Half_Adder half_adder_13 (.a(half_adder_12_carry), .b(a[12]), .sum(c[12]), .carry(half_adder_13_carry));
  Half_Adder half_adder_14 (.a(half_adder_13_carry), .b(a[13]), .sum(c[13]), .carry(half_adder_14_carry));
  Half_Adder half_adder_15 (.a(half_adder_14_carry), .b(a[14]), .sum(c[14]), .carry(half_adder_15_carry));
  Half_Adder half_adder_16 (.a(half_adder_15_carry), .b(a[15]), .sum(c[15]));  // open: carry
endmodule

module Multiplexer (
  input  _0,
  input  _1,
  input  sel,
  output out
);

  wire and_1_out, and_2_out;

  and and_1 (and_1_out, _0, ~sel);  // AND_Gate
  and and_2 (and_2_out, _1, sel);
  or or_1 (out, and_1_out, and_2_out);
endmodule

module Demultiplexer (
  input  in,
  input  sel,
  output _0,
  output _1
);

  and and_1 (_0, in, ~sel);  // AND_Gate
  and and_2 (_1, in, sel);
endmodule

module J_K_Flip_Flop_NOT_WORKING (
  input  J,
  input  K,
  output out
);

  wire and_1_out, and_2_out, clock_1_out, nor_1_out;

  Clock clock_1 (.out(clock_1_out));
  and and_1 (and_1_out, nor_1_out, J, clock_1_out);
  and and_2 (and_2_out, clock_1_out, K, out);
  nor nor_1 (nor_1_out, and_1_out, out);
  nor nor_2 (out, nor_1_out, and_2_out);
endmodule

module BCD_to_7segment (
  input  [3:0] BCD,
  output [6:0] Dispaly_Out
);

  wire and_1_out, and_2_out, and_3_out, and_4_out, and_5_out, and_6_out, and_7_out, and_8_out, and_9_out,
       buffer_1_out, buffer_2_out, buffer_3_out, buffer_4_out, not_1_out, not_2_out, not_3_out;

  buf buffer_1 (buffer_1_out, BCD[3]);
  buf buffer_2 (buffer_2_out, BCD[2]);
  not not_1 (not_1_out, BCD[2]);
  not not_2 (not_2_out, BCD[1]);
  buf buffer_3 (buffer_3_out, BCD[1]);
  buf buffer_4 (buffer_4_out, BCD[0]);
  not not_3 (not_3_out, BCD[0]);
  and and_1 (and_1_out, buffer_2_out, not_2_out);
  and and_2 (and_2_out, buffer_2_out, not_3_out);
  and and_3 (and_3_out, buffer_2_out, buffer_4_out);
  and and_4 (and_4_out, not_1_out, not_3_out);
  and and_5 (and_5_out, buffer_3_out, buffer_4_out);
  and and_6 (and_6_out, not_2_out, not_3_out);
  and and_7 (and_7_out, buffer_3_out, not_3_out);
  and and_8 (and_8_out, not_1_out, buffer_3_out);
  and and_9 (and_9_out, buffer_4_out, and_1_out);
  or or_1 (Dispaly_Out[0], and_3_out, and_4_out, buffer_1_out, buffer_3_out);
  or or_2 (Dispaly_Out[1], and_5_out, and_6_out, not_1_out);
  or or_3 (Dispaly_Out[2], buffer_2_out, not_2_out, buffer_4_out);
  or or_4 (Dispaly_Out[3], buffer_1_out, and_4_out, and_7_out, and_8_out, and_9_out);
  or or_5 (Dispaly_Out[4], and_7_out, and_4_out);
  or or_6 (Dispaly_Out[5], and_6_out, and_2_out, and_1_out, buffer_1_out);
  or or_7 (Dispaly_Out[6], and_7_out, and_1_out, buffer_1_out, and_8_out);
  _7_Segment_Display u_7_segment_display_1 (
    .g(Dispaly_Out[6]), .f(Dispaly_Out[5]), .a(Dispaly_Out[0]), .b(Dispaly_Out[1]), .e(Dispaly_Out[4]),
    .d(Dispaly_Out[3]), .c(Dispaly_Out[2]));  // open: dp

  // Notes on the sheet:
  //   X
  //   X Y Z W
  //   Y
  //   Z
  //   W
endmodule

module _8bit2BCD (
  input  [7:0] in_1,
  output [3:0] out_2,
  output [3:0] out_3,
  output [3:0] out_4
);

  wire add3_1_out_5, add3_1_out_6, add3_1_out_7, add3_1_out_8, add3_2_out_5, add3_2_out_6, add3_2_out_7,
       add3_2_out_8, add3_3_out_5, add3_3_out_6, add3_3_out_7, add3_3_out_8, add3_4_out_5, add3_4_out_6,
       add3_4_out_7, add3_5_out_5, add3_5_out_6, add3_5_out_7, add3_5_out_8;

  add3 add3_1 (
    .in_1(in_1[5]), .out_5(add3_1_out_5), .out_6(add3_1_out_6), .out_7(add3_1_out_7), .out_8(add3_1_out_8),
    .in_4(1'b0), .in_3(in_1[7]), .in_2(in_1[6]));
  add3 add3_2 (
    .in_1(in_1[4]), .out_5(add3_2_out_5), .out_6(add3_2_out_6), .out_7(add3_2_out_7), .out_8(add3_2_out_8),
    .in_4(add3_1_out_7), .in_3(add3_1_out_6), .in_2(add3_1_out_5));
  add3 add3_3 (
    .in_1(in_1[3]), .out_5(add3_3_out_5), .out_6(add3_3_out_6), .out_7(add3_3_out_7), .out_8(add3_3_out_8),
    .in_4(add3_2_out_7), .in_3(add3_2_out_6), .in_2(add3_2_out_5));
  add3 add3_4 (
    .in_1(add3_3_out_8), .out_5(add3_4_out_5), .out_6(add3_4_out_6), .out_7(add3_4_out_7), .out_8(out_4[1]),
    .in_4(1'b0), .in_3(add3_1_out_8), .in_2(add3_2_out_8));
  add3 add3_5 (
    .in_1(in_1[2]), .out_5(add3_5_out_5), .out_6(add3_5_out_6), .out_7(add3_5_out_7), .out_8(add3_5_out_8),
    .in_4(add3_3_out_7), .in_3(add3_3_out_6), .in_2(add3_3_out_5));
  add3 add3_6 (
    .in_1(add3_5_out_8), .out_5(out_3[1]), .out_6(out_3[2]), .out_7(out_3[3]), .out_8(out_4[0]),
    .in_4(add3_4_out_7), .in_3(add3_4_out_6), .in_2(add3_4_out_5));
  add3 add3_7 (
    .in_1(in_1[1]), .out_5(out_2[1]), .out_6(out_2[2]), .out_7(out_2[3]), .out_8(out_3[0]),
    .in_4(add3_5_out_7), .in_3(add3_5_out_6), .in_2(add3_5_out_5));

  assign out_2[0] = in_1[0];
  assign out_4[3:2] = 2'b00;
endmodule

module _8bit_Adder (
  input  [7:0] in_1,
  input  [7:0] in_2,
  output [7:0] out_3
);

  wire full_adder_1_carry, full_adder_2_carry, full_adder_3_carry, full_adder_4_carry, full_adder_5_carry,
       full_adder_6_carry, full_adder_7_carry;

  Full_Adder full_adder_1 (.a(in_1[0]), .b(1'b0), .c(in_2[0]), .sum(out_3[0]), .carry(full_adder_1_carry));
  Full_Adder full_adder_2 (
    .a(full_adder_1_carry), .b(in_1[1]), .c(in_2[1]), .sum(out_3[1]), .carry(full_adder_2_carry));
  Full_Adder full_adder_3 (
    .a(full_adder_2_carry), .b(in_1[2]), .c(in_2[2]), .sum(out_3[2]), .carry(full_adder_3_carry));
  Full_Adder full_adder_4 (
    .a(full_adder_3_carry), .b(in_1[3]), .c(in_2[3]), .sum(out_3[3]), .carry(full_adder_4_carry));
  Full_Adder full_adder_5 (
    .a(full_adder_4_carry), .b(in_1[4]), .c(in_2[4]), .sum(out_3[4]), .carry(full_adder_5_carry));
  Full_Adder full_adder_6 (
    .a(full_adder_5_carry), .b(in_1[5]), .c(in_2[5]), .sum(out_3[5]), .carry(full_adder_6_carry));
  Full_Adder full_adder_7 (
    .a(full_adder_6_carry), .b(in_1[6]), .c(in_2[6]), .sum(out_3[6]), .carry(full_adder_7_carry));
  Full_Adder full_adder_8 (.a(full_adder_7_carry), .b(in_1[7]), .c(in_2[7]), .sum(out_3[7]));  // open: carry
endmodule

module add3 (
  input  in_1,
  input  in_2,
  input  in_3,
  input  in_4,
  output out_5,
  output out_6,
  output out_7,
  output out_8
);

  wire and_1_out, full_adder_1_carry, full_adder_2_carry, full_adder_3_carry, or_1_out, or_2_out;

  or or_1 (or_1_out, in_4, and_1_out);
  and and_1 (and_1_out, in_3, or_2_out);
  or or_2 (or_2_out, in_2, in_1);
  Full_Adder full_adder_1 (.a(1'b0), .b(in_1), .c(or_1_out), .sum(out_5), .carry(full_adder_1_carry));
  Full_Adder full_adder_2 (.a(full_adder_1_carry), .b(in_2), .c(or_1_out), .sum(out_6), .carry(full_adder_2_carry));
  Full_Adder full_adder_3 (.a(full_adder_2_carry), .b(in_3), .c(1'b0), .sum(out_7), .carry(full_adder_3_carry));
  Full_Adder full_adder_4 (.a(full_adder_3_carry), .b(in_4), .c(1'b0), .sum(out_8));  // open: carry
endmodule

module CPU (
  input  cl,
  input  [15:0] Instruction,
  input  [15:0] Data_Memory,
  input  Reset,
  output [15:0] outM,
  output writeM,
  output [14:0] addressM,
  output [14:0] pc
);

  wire A, a_t, and_2_out, and_3_out, and_4_out, and_5_out, and_6_out, and_7_out, and_8_out, and_9_out,
       and_10_out, and_11_out, and_12_out, clock_1_out, D, esc, Inc, ins_type, J1, J2, J3, JM, N, nand_1_out,
       nand_2_out, nand_3_out, not_1_out, not_2_out, not_4_out, or_1_out, or_2_out, or_3_out, Z;
  wire [5:0] ins;
  wire [14:13] multiplexer_1_out;
  wire [15:0] alu_1_y_2, multiplexer_2_out, multiplexer_3_out, n16bit_register_2_out_4;
  wire [15:15] n16bit_register_1_out_4;

  and and_1 (esc, ins_type, not_1_out);
  not not_1 (not_1_out, multiplexer_1_out[14]);
  // Probe on {ins_type, multiplexer_1_out, a_t, ins[0], ins[1], ins[2], ins[3], ins[4], ins[5], A, D, writeM, J1, J2, J3}
  Multiplexer_part #(.width(16), .disabled(0)) multiplexer_1 (
    .in1(Instruction),
    .out({ins_type, multiplexer_1_out, a_t, ins[0], ins[1], ins[2], ins[3], ins[4], ins[5], A, D, writeM, J1, J2, J3}),
    .sel(Instruction[15]), .en(Instruction[15]));  // open: in0
  nand nand_1 (nand_1_out, J1, J2);
  nand nand_2 (nand_2_out, J1, J3);
  and and_2 (and_2_out, J3, J2);
  nand nand_3 (nand_3_out, J2, J3);
  and and_3 (and_3_out, J1, J3);
  and and_4 (and_4_out, J1, J2);
  and and_5 (and_5_out, J1, J2, J3);
  and and_6 (and_6_out, ~Z, nand_1_out, J3, ~N);  // AND_Gate
  and and_7 (and_7_out, nand_2_out, Z, J2);
  or or_1 (or_1_out, ~N, Z);  // OR_Gate
  and and_8 (and_8_out, N, nand_3_out, J1, ~Z);  // AND_Gate
  and and_9 (and_9_out, and_3_out, ~Z, ~J2);  // AND_Gate
  and and_10 (and_10_out, and_4_out, or_2_out, ~J3);  // AND_Gate
  or or_2 (or_2_out, N, Z);
  not not_2 (not_2_out, Instruction[15]);
  // Probe on Instruction
  and and_11 (and_11_out, and_2_out, or_1_out, ~J3);  // AND_Gate
  or or_3 (or_3_out, not_2_out, A);
  Multiplexer_part #(.width(16), .enable("false")) multiplexer_2 (
    .in0(outM), .in1(Instruction), .out(multiplexer_2_out), .sel(not_2_out));
  not not_3 (Inc, JM);
  or or_4 (JM, and_6_out, and_7_out, and_11_out, and_8_out, and_9_out, and_10_out, and_5_out);
  _16bit_Register u_16bit_register_1 (
    .in_3(multiplexer_2_out), .out_4({n16bit_register_1_out_4[15], addressM}), .load(or_3_out), .cl(not_4_out));
  // Probe on {n16bit_register_1_out_4[15], addressM}
  Clock clock_1 (.out(clock_1_out));
  not not_4 (not_4_out, clock_1_out);
  _16bit_Register u_16bit_register_2 (.in_3(outM), .out_4(n16bit_register_2_out_4), .load(D), .cl(not_4_out));
  Multiplexer_part #(.width(16), .enable("false")) multiplexer_3 (
    .in0({n16bit_register_1_out_4[15], addressM}), .in1(Data_Memory), .out(multiplexer_3_out), .sel(a_t));
  // Probe on multiplexer_3_out
  and and_12 (and_12_out, Inc, ~esc);  // AND_Gate
  Counter counter_1 (.in(addressM), .out(pc), .inc(and_12_out), .load(JM), .clr(Reset));
  // Probe on n16bit_register_2_out_4
  ALU alu_1 (
    .x(n16bit_register_2_out_4), .y(multiplexer_3_out), .y_2(alu_1_y_2), .zx(ins[0]), .zy(ins[2]),
    .nx(ins[1]), .ny(ins[3]), .f(ins[4]), .no(ins[5]), .zr(Z), .ng(N));
  // Probe on pc
  // Probe on outM
  _16bit_Register u_16bit_register_3 (.in_3(alu_1_y_2), .out_4(outM), .load(clock_1_out), .cl(clock_1_out));

  // Other names for the same wires on the sheet: M = writeM

  // Notes on the sheet:
  //   ALU output
  //   A register
  //   D register
  //   ALU output
endmodule

module Memory (
);

  wire undriven;

  RAM #(.bus("separate")) ram_1 (.sel(undriven));  // open: addr, din, data, str, clk, ld, clr
  RAM #(.bus("separate")) ram_2 ();  // open: addr, din, data, str, sel, clk, ld, clr
  _16bit_Register u_16bit_register_1 ();  // open: in_3, out_4, load, cl
endmodule

module add3_better (
  input  a,
  input  b,
  input  c,
  input  d,
  output x,
  output y,
  output z,
  output u
);

  // NOT_Gate not_1 has open pins: in=a, out=open
  // NOT_Gate not_2 has open pins: in=b, out=open
  // NOT_Gate not_3 has open pins: in=c, out=open
  // NOT_Gate not_4 has open pins: in=d, out=open
endmodule

module Display (
  input  [15:0] in_1,
  output out_2,
  output out_3,
  output out_4,
  output out_5,
  output out_6,
  output out_7,
  output out_8,
  output out_9,
  output out_10,
  output out_11,
  output out_12,
  output out_13,
  output out_14,
  output out_15,
  output out_16,
  output out_17,
  output out_18,
  output out_19,
  output out_20,
  output out_21,
  output out_22,
  output out_23,
  output out_24,
  output out_25,
  output out_26,
  output out_27,
  output out_28,
  output out_29,
  output out_30,
  output out_31,
  output out_32,
  output out_33,
  output out_34,
  output out_35,
  output out_36,
  output out_37,
  output out_38,
  output out_39,
  output out_40,
  output out_41
);

  wire [3:0] n16bit2bcd_1_out_2, n16bit2bcd_1_out_3, n16bit2bcd_1_out_4, n16bit2bcd_1_out_5,
       n16bit2bcd_1_out_6;

  _16bit2BCD u_16bit2bcd_1 (
    .in_1(in_1), .out_2(n16bit2bcd_1_out_2), .out_3(n16bit2bcd_1_out_3), .out_4(n16bit2bcd_1_out_4),
    .out_5(n16bit2bcd_1_out_5), .out_6(n16bit2bcd_1_out_6));
  BCD_to_7segment bcd_to_7segment_1 (
    .BCD(n16bit2bcd_1_out_2), .Dispaly_Out({out_18, out_19, out_38, out_39, out_40, out_21, out_20}));
  BCD_to_7segment bcd_to_7segment_2 (
    .BCD(n16bit2bcd_1_out_3), .Dispaly_Out({out_14, out_15, out_34, out_35, out_36, out_17, out_16}));
  BCD_to_7segment bcd_to_7segment_3 (
    .BCD(n16bit2bcd_1_out_4), .Dispaly_Out({out_10, out_11, out_30, out_31, out_32, out_13, out_12}));
  BCD_to_7segment bcd_to_7segment_4 (
    .BCD(n16bit2bcd_1_out_5), .Dispaly_Out({out_6, out_7, out_26, out_27, out_28, out_9, out_8}));
  BCD_to_7segment bcd_to_7segment_5 (
    .BCD(n16bit2bcd_1_out_6), .Dispaly_Out({out_2, out_3, out_22, out_23, out_24, out_5, out_4}));
endmodule

module _16bit2BCD (
  input  [15:0] in_1,
  output [3:0] out_2,
  output [3:0] out_3,
  output [3:0] out_4,
  output [3:0] out_5,
  output [3:0] out_6
);

  wire add3_1_out_5, add3_1_out_6, add3_1_out_7, add3_2_out_5, add3_2_out_6, add3_2_out_7, add3_2_out_8,
       add3_3_out_5, add3_3_out_6, add3_3_out_7, add3_3_out_8, add3_4_out_5, add3_4_out_6, add3_4_out_7,
       add3_4_out_8, add3_5_out_5, add3_5_out_6, add3_5_out_7, add3_5_out_8, add3_6_out_5, add3_6_out_6,
       add3_6_out_7, add3_6_out_8, add3_7_out_5, add3_7_out_6, add3_7_out_7, add3_7_out_8, add3_8_out_5,
       add3_8_out_6, add3_8_out_7, add3_8_out_8, add3_9_out_5, add3_9_out_6, add3_9_out_7, add3_9_out_8,
       add3_10_out_5, add3_10_out_6, add3_10_out_7, add3_10_out_8, add3_11_out_5, add3_11_out_6,
       add3_11_out_7, add3_11_out_8, add3_12_out_5, add3_12_out_6, add3_12_out_7, add3_12_out_8,
       add3_13_out_5, add3_13_out_6, add3_13_out_7, add3_13_out_8, add3_14_out_5, add3_14_out_6,
       add3_14_out_7, add3_14_out_8, add3_15_out_5, add3_15_out_6, add3_15_out_7, add3_15_out_8,
       add3_16_out_5, add3_16_out_6, add3_16_out_7, add3_16_out_8, add3_17_out_5, add3_17_out_6,
       add3_17_out_7, add3_17_out_8, add3_18_out_5, add3_18_out_6, add3_18_out_7, add3_18_out_8,
       add3_19_out_5, add3_19_out_6, add3_19_out_7, add3_19_out_8, add3_20_out_5, add3_20_out_6,
       add3_20_out_7, add3_21_out_5, add3_21_out_6, add3_21_out_7, add3_21_out_8, add3_22_out_5,
       add3_22_out_6, add3_22_out_7, add3_25_out_5, add3_25_out_6, add3_25_out_7, add3_25_out_8,
       add3_26_out_5, add3_26_out_6, add3_26_out_7, add3_26_out_8, add3_27_out_5, add3_27_out_6,
       add3_27_out_7, add3_27_out_8, add3_28_out_5, add3_28_out_6, add3_28_out_7, add3_28_out_8,
       add3_29_out_5, add3_29_out_6, add3_29_out_7, add3_29_out_8, add3_30_out_5, add3_30_out_6,
       add3_30_out_7, add3_30_out_8, add3_31_out_5, add3_31_out_6, add3_31_out_7, add3_31_out_8,
       add3_32_out_5, add3_32_out_6, add3_32_out_7, add3_32_out_8;

  add3 add3_1 (
    .in_1(add3_15_out_8), .out_5(add3_1_out_5), .out_6(add3_1_out_6), .out_7(add3_1_out_7), .out_8(out_6[3]),
    .in_4(1'b0), .in_3(add3_11_out_8), .in_2(add3_14_out_8));
  add3 add3_2 (
    .in_1(in_1[13]), .out_5(add3_2_out_5), .out_6(add3_2_out_6), .out_7(add3_2_out_7), .out_8(add3_2_out_8),
    .in_4(1'b0), .in_3(in_1[15]), .in_2(in_1[14]));
  add3 add3_3 (
    .in_1(in_1[12]), .out_5(add3_3_out_5), .out_6(add3_3_out_6), .out_7(add3_3_out_7), .out_8(add3_3_out_8),
    .in_4(add3_2_out_7), .in_3(add3_2_out_6), .in_2(add3_2_out_5));
  add3 add3_4 (
    .in_1(in_1[11]), .out_5(add3_4_out_5), .out_6(add3_4_out_6), .out_7(add3_4_out_7), .out_8(add3_4_out_8),
    .in_4(add3_3_out_7), .in_3(add3_3_out_6), .in_2(add3_3_out_5));
  add3 add3_5 (
    .in_1(add3_4_out_8), .out_5(add3_5_out_5), .out_6(add3_5_out_6), .out_7(add3_5_out_7),
    .out_8(add3_5_out_8), .in_4(1'b0), .in_3(add3_2_out_8), .in_2(add3_3_out_8));
  add3 add3_6 (
    .in_1(in_1[10]), .out_5(add3_6_out_5), .out_6(add3_6_out_6), .out_7(add3_6_out_7), .out_8(add3_6_out_8),
    .in_4(add3_4_out_7), .in_3(add3_4_out_6), .in_2(add3_4_out_5));
  add3 add3_7 (
    .in_1(add3_6_out_8), .out_5(add3_7_out_5), .out_6(add3_7_out_6), .out_7(add3_7_out_7),
    .out_8(add3_7_out_8), .in_4(add3_5_out_7), .in_3(add3_5_out_6), .in_2(add3_5_out_5));
  add3 add3_8 (
    .in_1(in_1[9]), .out_5(add3_8_out_5), .out_6(add3_8_out_6), .out_7(add3_8_out_7), .out_8(add3_8_out_8),
    .in_4(add3_6_out_7), .in_3(add3_6_out_6), .in_2(add3_6_out_5));
  add3 add3_9 (
    .in_1(add3_8_out_8), .out_5(add3_9_out_5), .out_6(add3_9_out_6), .out_7(add3_9_out_7),
    .out_8(add3_9_out_8), .in_4(add3_7_out_7), .in_3(add3_7_out_6), .in_2(add3_7_out_5));
  add3 add3_10 (
    .in_1(in_1[8]), .out_5(add3_10_out_5), .out_6(add3_10_out_6), .out_7(add3_10_out_7),
    .out_8(add3_10_out_8), .in_4(add3_8_out_7), .in_3(add3_8_out_6), .in_2(add3_8_out_5));
  add3 add3_11 (
    .in_1(add3_9_out_8), .out_5(add3_11_out_5), .out_6(add3_11_out_6), .out_7(add3_11_out_7),
    .out_8(add3_11_out_8), .in_4(1'b0), .in_3(add3_5_out_8), .in_2(add3_7_out_8));
  add3 add3_12 (
    .in_1(add3_10_out_8), .out_5(add3_12_out_5), .out_6(add3_12_out_6), .out_7(add3_12_out_7),
    .out_8(add3_12_out_8), .in_4(add3_9_out_7), .in_3(add3_9_out_6), .in_2(add3_9_out_5));
  add3 add3_13 (
    .in_1(add3_25_out_8), .out_5(add3_13_out_5), .out_6(add3_13_out_6), .out_7(add3_13_out_7),
    .out_8(add3_13_out_8), .in_4(add3_12_out_7), .in_3(add3_12_out_6), .in_2(add3_12_out_5));
  add3 add3_14 (
    .in_1(add3_12_out_8), .out_5(add3_14_out_5), .out_6(add3_14_out_6), .out_7(add3_14_out_7),
    .out_8(add3_14_out_8), .in_4(add3_11_out_7), .in_3(add3_11_out_6), .in_2(add3_11_out_5));
  add3 add3_15 (
    .in_1(add3_13_out_8), .out_5(add3_15_out_5), .out_6(add3_15_out_6), .out_7(add3_15_out_7),
    .out_8(add3_15_out_8), .in_4(add3_14_out_7), .in_3(add3_14_out_6), .in_2(add3_14_out_5));
  add3 add3_16 (
    .in_1(add3_26_out_8), .out_5(add3_16_out_5), .out_6(add3_16_out_6), .out_7(add3_16_out_7),
    .out_8(add3_16_out_8), .in_4(add3_13_out_7), .in_3(add3_13_out_6), .in_2(add3_13_out_5));
  add3 add3_17 (
    .in_1(add3_16_out_8), .out_5(add3_17_out_5), .out_6(add3_17_out_6), .out_7(add3_17_out_7),
    .out_8(add3_17_out_8), .in_4(add3_15_out_7), .in_3(add3_15_out_6), .in_2(add3_15_out_5));
  add3 add3_18 (
    .in_1(add3_27_out_8), .out_5(add3_18_out_5), .out_6(add3_18_out_6), .out_7(add3_18_out_7),
    .out_8(add3_18_out_8), .in_4(add3_16_out_7), .in_3(add3_16_out_6), .in_2(add3_16_out_5));
  add3 add3_19 (
    .in_1(add3_18_out_8), .out_5(add3_19_out_5), .out_6(add3_19_out_6), .out_7(add3_19_out_7),
    .out_8(add3_19_out_8), .in_4(add3_17_out_7), .in_3(add3_17_out_6), .in_2(add3_17_out_5));
  add3 add3_20 (
    .in_1(add3_17_out_8), .out_5(add3_20_out_5), .out_6(add3_20_out_6), .out_7(add3_20_out_7),
    .out_8(out_6[2]), .in_4(add3_1_out_7), .in_3(add3_1_out_6), .in_2(add3_1_out_5));
  add3 add3_21 (
    .in_1(add3_30_out_8), .out_5(add3_21_out_5), .out_6(add3_21_out_6), .out_7(add3_21_out_7),
    .out_8(add3_21_out_8), .in_4(add3_19_out_7), .in_3(add3_19_out_6), .in_2(add3_19_out_5));
  add3 add3_22 (
    .in_1(add3_19_out_8), .out_5(add3_22_out_5), .out_6(add3_22_out_6), .out_7(add3_22_out_7),
    .out_8(out_6[1]), .in_4(add3_20_out_7), .in_3(add3_20_out_6), .in_2(add3_20_out_5));
  add3 add3_23 (
    .in_1(add3_32_out_8), .out_5(out_4[1]), .out_6(out_4[2]), .out_7(out_4[3]), .out_8(out_5[0]),
    .in_4(add3_21_out_7), .in_3(add3_21_out_6), .in_2(add3_21_out_5));
  add3 add3_24 (
    .in_1(add3_21_out_8), .out_5(out_5[1]), .out_6(out_5[2]), .out_7(out_5[3]), .out_8(out_6[0]),
    .in_4(add3_22_out_7), .in_3(add3_22_out_6), .in_2(add3_22_out_5));
  add3 add3_25 (
    .in_1(in_1[7]), .out_5(add3_25_out_5), .out_6(add3_25_out_6), .out_7(add3_25_out_7),
    .out_8(add3_25_out_8), .in_4(add3_10_out_7), .in_3(add3_10_out_6), .in_2(add3_10_out_5));
  add3 add3_26 (
    .in_1(in_1[6]), .out_5(add3_26_out_5), .out_6(add3_26_out_6), .out_7(add3_26_out_7),
    .out_8(add3_26_out_8), .in_4(add3_25_out_7), .in_3(add3_25_out_6), .in_2(add3_25_out_5));
  add3 add3_27 (
    .in_1(in_1[5]), .out_5(add3_27_out_5), .out_6(add3_27_out_6), .out_7(add3_27_out_7),
    .out_8(add3_27_out_8), .in_4(add3_26_out_7), .in_3(add3_26_out_6), .in_2(add3_26_out_5));
  add3 add3_28 (
    .in_1(in_1[4]), .out_5(add3_28_out_5), .out_6(add3_28_out_6), .out_7(add3_28_out_7),
    .out_8(add3_28_out_8), .in_4(add3_27_out_7), .in_3(add3_27_out_6), .in_2(add3_27_out_5));
  add3 add3_29 (
    .in_1(in_1[3]), .out_5(add3_29_out_5), .out_6(add3_29_out_6), .out_7(add3_29_out_7),
    .out_8(add3_29_out_8), .in_4(add3_28_out_7), .in_3(add3_28_out_6), .in_2(add3_28_out_5));
  add3 add3_30 (
    .in_1(add3_28_out_8), .out_5(add3_30_out_5), .out_6(add3_30_out_6), .out_7(add3_30_out_7),
    .out_8(add3_30_out_8), .in_4(add3_18_out_7), .in_3(add3_18_out_6), .in_2(add3_18_out_5));
  add3 add3_31 (
    .in_1(in_1[2]), .out_5(add3_31_out_5), .out_6(add3_31_out_6), .out_7(add3_31_out_7),
    .out_8(add3_31_out_8), .in_4(add3_29_out_7), .in_3(add3_29_out_6), .in_2(add3_29_out_5));
  add3 add3_32 (
    .in_1(add3_29_out_8), .out_5(add3_32_out_5), .out_6(add3_32_out_6), .out_7(add3_32_out_7),
    .out_8(add3_32_out_8), .in_4(add3_30_out_7), .in_3(add3_30_out_6), .in_2(add3_30_out_5));
  add3 add3_33 (
    .in_1(add3_31_out_8), .out_5(out_3[1]), .out_6(out_3[2]), .out_7(out_3[3]), .out_8(out_4[0]),
    .in_4(add3_32_out_7), .in_3(add3_32_out_6), .in_2(add3_32_out_5));
  add3 add3_34 (
    .in_1(in_1[1]), .out_5(out_2[1]), .out_6(out_2[2]), .out_7(out_2[3]), .out_8(out_3[0]),
    .in_4(add3_31_out_7), .in_3(add3_31_out_6), .in_2(add3_31_out_5));

  assign out_2[0] = in_1[0];
endmodule
